// Logisim project ALU.circ as structural Verilog: 5 circuits, main circuit ALU
module half_adder (
  input  A,
  input  B,
  output sum,
  output carry
);

  xor xor_1 (sum, A, B);
  and and_1 (carry, A, B);
endmodule

module full_adder (
  input  A,
  input  B,
  input  CIn,
  output SUM,
  output Cout
);

  wire half_adder_1_carry, half_adder_1_sum, half_adder_2_carry;

  half_adder half_adder_1 (.A(A), .B(B), .sum(half_adder_1_sum), .carry(half_adder_1_carry));
  half_adder half_adder_2 (.A(half_adder_1_sum), .B(CIn), .sum(SUM), .carry(half_adder_2_carry));
  or or_1 (Cout, half_adder_1_carry, half_adder_2_carry);
endmodule

module _4_bit_adder (
  input  A0,
  input  A1,
  input  A2,
  input  A3,
  input  B0,
  input  B1,
  input  B2,
  input  B3,
  output S0,
  output S1,
  output S2,
  output S3,
  output COUT
);

  wire full_adder_1_cout, full_adder_2_cout, half_adder_1_carry;

  half_adder half_adder_1 (.A(A0), .B(B0), .sum(S0), .carry(half_adder_1_carry));
  full_adder full_adder_1 (.A(A1), .B(B1), .CIn(half_adder_1_carry), .SUM(S1), .Cout(full_adder_1_cout));
  full_adder full_adder_2 (.A(A2), .B(B2), .CIn(full_adder_1_cout), .SUM(S2), .Cout(full_adder_2_cout));
  full_adder full_adder_3 (.A(A3), .B(B3), .CIn(full_adder_2_cout), .SUM(S3), .Cout(COUT));
endmodule

module ALU (
  input  [3:0] Adata,
  input  [3:0] Bdata,
  input  ctr,
  output [3:0] dataout,
  output sign,
  output zero,
  output carry,
  output overflow,
  output Negative
);

  wire n4_bit_adder_1_s0, n4_bit_adder_1_s1, n4_bit_adder_1_s2, n4_bit_adder_1_s3, n4_bit_adder_2_0_1_cx,
       not_1_out, not_2_out, not_3_out, not_4_out, not_5_out, xnor_1_out, xor_1_out, xor_2_out, xor_3_out,
       xor_4_out;

  xor xor_1 (xor_1_out, ctr, Bdata[0]);
  xor xor_2 (xor_2_out, ctr, Bdata[1]);
  xor xor_3 (xor_3_out, ctr, Bdata[2]);
  xor xor_4 (xor_4_out, ctr, Bdata[3]);
  _4_bit_adder u_4_bit_adder_1 (
    .A0(xor_1_out), .A1(xor_2_out), .A2(xor_3_out), .A3(xor_4_out), .B0(ctr), .B1(1'b0), .B2(1'b0),
    .B3(1'b0), .S0(n4_bit_adder_1_s0), .S1(n4_bit_adder_1_s1), .S2(n4_bit_adder_1_s2), .S3(n4_bit_adder_1_s3));  // open: COUT
  _4_BIT_ADDER_2_0 u_4_bit_adder_2_0_1 (
    .A0(Adata[0]), .A1(Adata[1]), .A2(Adata[2]), .A3(Adata[3]), .B0(n4_bit_adder_1_s0),
    .B1(n4_bit_adder_1_s1), .B2(n4_bit_adder_1_s2), .B3(n4_bit_adder_1_s3), .S0(dataout[0]), .S2(dataout[1]),
    .S2_2(dataout[2]), .S3(dataout[3]), .COUT(carry), .CX(n4_bit_adder_2_0_1_cx));
  xnor xnor_1 (xnor_1_out, Adata[3], n4_bit_adder_1_s3);
  not not_1 (not_1_out, carry);
  and and_1 (overflow, n4_bit_adder_2_0_1_cx, xnor_1_out);
  and and_2 (Negative, not_1_out, ctr);
  not not_2 (not_2_out, dataout[0]);
  not not_3 (not_3_out, dataout[1]);
  not not_4 (not_4_out, dataout[2]);
  not not_5 (not_5_out, dataout[3]);
  ExactlyOne xor_5 (.out(sign), .in1(dataout[3]), .in2(overflow), .in3(overflow), .in4(overflow));
  and and_3 (zero, not_2_out, not_3_out, not_4_out, not_5_out);

  // Notes on the sheet:
  //   1 for sub
  //   0 for add
endmodule

module _4_BIT_ADDER_2_0 (
  input  A0,
  input  A1,
  input  A2,
  input  A3,
  input  B0,
  input  B1,
  input  B2,
  input  B3,
  output S0,
  output S2,
  output S2_2,
  output S3,
  output COUT,
  output CX
);

  wire full_adder_1_cout, half_adder_1_carry;

  half_adder half_adder_1 (.A(A0), .B(B0), .sum(S0), .carry(half_adder_1_carry));
  full_adder full_adder_1 (.A(A1), .B(B1), .CIn(half_adder_1_carry), .SUM(S2), .Cout(full_adder_1_cout));
  full_adder full_adder_2 (.A(A2), .B(B2), .CIn(full_adder_1_cout), .SUM(S2_2), .Cout(CX));
  full_adder full_adder_3 (.A(A3), .B(B3), .CIn(CX), .SUM(S3), .Cout(COUT));

  // Notes on the sheet:
  //   needed for overflow flag
endmodule
