// Logisim project registersgpr.circ as structural Verilog: 1 circuit, main circuit main
module main (
);

  wire and_1_out, and_2_out, and_3_out, and_4_out, and_5_out, and_6_out, and_7_out, and_8_out,
       decoder_1_out0, decoder_1_out1, decoder_1_out2, decoder_1_out3, decoder_1_out4, decoder_1_out5,
       decoder_1_out6, decoder_1_out7, nor_1_out, undriven, undriven_2, undriven_4, undriven_5, undriven_7,
       undriven_8;
  wire [2:0] undriven_3;
  wire [3:0] controlled_buffer_1_out, controlled_buffer_2_out, controlled_buffer_3_out,
       controlled_buffer_4_out, controlled_buffer_5_out, controlled_buffer_9_out, controlled_buffer_10_out,
       controlled_buffer_11_out, controlled_buffer_12_out, register_1_q, register_2_q, register_3_q,
       register_4_q, register_5_q, register_6_q, register_7_q, register_8_q, undriven_6;

  nor nor_1 (nor_1_out, undriven, undriven_2);
  Decoder #(.select(3)) decoder_1 (
    .out0(decoder_1_out0), .out1(decoder_1_out1), .out2(decoder_1_out2), .out3(decoder_1_out3),
    .out4(decoder_1_out4), .out5(decoder_1_out5), .out6(decoder_1_out6), .out7(decoder_1_out7),
    .sel(undriven_3), .en(nor_1_out));
  and and_1 (and_1_out, undriven_4, decoder_1_out0);
  assign controlled_buffer_1_out = undriven_5 ? undriven_6 : 4'bz;  // Controlled_Buffer controlled_buffer_1
  and and_2 (and_2_out, undriven_4, decoder_1_out2);
  assign controlled_buffer_2_out = undriven_5 ? undriven_6 : 4'bz;  // Controlled_Buffer controlled_buffer_2
  and and_3 (and_3_out, undriven_4, decoder_1_out4);
  assign controlled_buffer_3_out = undriven_5 ? undriven_6 : 4'bz;  // Controlled_Buffer controlled_buffer_3
  and and_4 (and_4_out, undriven_4, decoder_1_out6);
  assign controlled_buffer_4_out = undriven_5 ? undriven_6 : 4'bz;  // Controlled_Buffer controlled_buffer_4
  Register #(.width(4)) register_1 (
    .D(controlled_buffer_1_out), .en(decoder_1_out0), .Q(register_1_q), .clk(undriven_7), .clr(undriven_8));
  Register #(.width(4)) register_2 (
    .D(controlled_buffer_2_out), .en(decoder_1_out2), .Q(register_2_q), .clk(undriven_7), .clr(undriven_8));
  Register #(.width(4)) register_3 (
    .D(controlled_buffer_3_out), .en(decoder_1_out4), .Q(register_3_q), .clk(undriven_7), .clr(undriven_8));
  Register #(.width(4)) register_4 (
    .D(controlled_buffer_4_out), .en(decoder_1_out6), .Q(register_4_q), .clk(undriven_7), .clr(undriven_8));
  assign controlled_buffer_5_out = and_1_out ? register_1_q : 4'bz;  // Controlled_Buffer controlled_buffer_5
  assign controlled_buffer_5_out = and_2_out ? register_2_q : 4'bz;  // Controlled_Buffer controlled_buffer_6
  assign controlled_buffer_5_out = and_3_out ? register_3_q : 4'bz;  // Controlled_Buffer controlled_buffer_7
  assign controlled_buffer_5_out = and_4_out ? register_4_q : 4'bz;  // Controlled_Buffer controlled_buffer_8
  and and_5 (and_5_out, undriven_4, decoder_1_out1);
  assign controlled_buffer_9_out = undriven_5 ? undriven_6 : 4'bz;  // Controlled_Buffer controlled_buffer_9
  and and_6 (and_6_out, undriven_4, decoder_1_out3);
  assign controlled_buffer_10_out = undriven_5 ? undriven_6 : 4'bz;  // Controlled_Buffer controlled_buffer_10
  and and_7 (and_7_out, undriven_4, decoder_1_out5);
  assign controlled_buffer_11_out = undriven_5 ? undriven_6 : 4'bz;  // Controlled_Buffer controlled_buffer_11
  and and_8 (and_8_out, undriven_4, decoder_1_out7);
  assign controlled_buffer_12_out = undriven_5 ? undriven_6 : 4'bz;  // Controlled_Buffer controlled_buffer_12
  assign controlled_buffer_5_out = and_5_out ? register_5_q : 4'bz;  // Controlled_Buffer controlled_buffer_13
  Register #(.width(4)) register_5 (
    .D(controlled_buffer_9_out), .en(decoder_1_out1), .Q(register_5_q), .clk(undriven_7), .clr(undriven_8));
  assign controlled_buffer_5_out = and_6_out ? register_6_q : 4'bz;  // Controlled_Buffer controlled_buffer_14
  Register #(.width(4)) register_6 (
    .D(controlled_buffer_10_out), .en(decoder_1_out3), .Q(register_6_q), .clk(undriven_7), .clr(undriven_8));
  assign controlled_buffer_5_out = and_7_out ? register_7_q : 4'bz;  // Controlled_Buffer controlled_buffer_15
  Register #(.width(4)) register_7 (
    .D(controlled_buffer_11_out), .en(decoder_1_out5), .Q(register_7_q), .clk(undriven_7), .clr(undriven_8));
  Register #(.width(4)) register_8 (
    .D(controlled_buffer_12_out), .en(decoder_1_out7), .Q(register_8_q), .clk(undriven_7), .clr(undriven_8));
  assign controlled_buffer_5_out = and_8_out ? register_8_q : 4'bz;  // Controlled_Buffer controlled_buffer_16

  // Notes on the sheet:
  //   Address
  //   A4
  //   A3
  //   Data in
  //   Rin
  //   Rout
  //   clk
  //   reset
  //   Data out
endmodule
